# Fritzing sketch robot0 (saved by Fritzing 0.9.2b)
stripboards: 1

parts:
  Raspberry_Pi1 = Raspberry Pi 2
  Part1 = PowerBoost 500 Charger
  U1 = LIPO-2000mAh [package=lipo-2000]
  Part2 = SRF05 Ultrasonic Rangefinder
  Part3 = SRF05 Ultrasonic Rangefinder
  Part4 = SRF05 Ultrasonic Rangefinder
  GY2 = MPU-6050 Board GY-521 [form="♀ (female)" package=THT]
  R1 = Resistor [tolerance=±20% resistance=2.0k package="0805 [SMD]"]
  R2 = Resistor [tolerance=±5% resistance=1k package=THT]
  R3 = Resistor [tolerance=±5% resistance=1k package=THT]
  R4 = Resistor [tolerance=±20% resistance=2.0k package="0805 [SMD]"]
  R5 = Resistor [tolerance=±5% resistance=1k package=THT]
  R6 = Resistor [tolerance=±20% resistance=2.0k package="0805 [SMD]"]

nets:
  GND: Raspberry_Pi1.GPIO2, Part2.GND, Part3.GND, Part4.GND, GY2.pin1, GY2.pin2, R1.Pin_1, R4.Pin_1, R6.Pin_1
  N1: Part1.GND, U1.-
  N2: Part1.5.0V, U1.+
  VCC: Part2.VCC, Part3.VCC, Part4.VCC
  N3: Part2.Trig, Part3.Trig, R1.Pin_0, R2.Pin_1
  N4: Part2.Echo, R2.Pin_0
  N5: Part3.Echo, R3.Pin_0
  N6: Part4.Echo, R5.Pin_0
  N7: R3.Pin_1, R4.Pin_0
  N8: R5.Pin_1, R6.Pin_0

custom parts:
  PowerBoost 500 Charger: The PowerBoost 500C is a little DC/DC boost converter module that can be powered by any 3.7V LiIon/LiPoly battery, and convert the battery output to 5.2V DC for running your 5V projects. At its heart is a TPS61090 boost converter from TI. This boost converter chip has some really nice extras such as low battery detection, 2A internal switch, synchronous conversion, excellent efficiency, and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
  MPU-6050 Board GY-521: Acelerometro y Giroscopio MPU-6050 Board GY-521
