# Fritzing sketch sonars (saved by Fritzing 0.9.2b)
circuit board: 3.08262cm x 2.55017cm
stripboards: 2

parts:
  3_2_1_G_V = mystery part, 5 pins [chip_label=321GV]
  s1 = mystery part, 3 pins [chip_label=sonar1]
  s2 = mystery part, 3 pins [chip_label=sonar2]
  s3 = mystery part, 3 pins [chip_label=sonar3]
  g1 = Resistor [tolerance=±5% resistance=220 package=THT]
  e1 = Resistor [tolerance=±5% resistance=220 package=THT]
  e2 = Resistor [tolerance=±5% resistance=220 package=THT]
  g2 = Resistor [tolerance=±5% resistance=220 package=THT]
  g3 = Resistor [tolerance=±5% resistance=220 package=THT]
  e3 = Resistor [tolerance=±5% resistance=220 package=THT]

nets:
  N1: 3_2_1_G_V.pin1, s1.pin1, s2.pin1, s3.pin1
  N2: 3_2_1_G_V.pin2, s1.pin3, s2.pin3, s3.pin3, g1.Pin_1, g2.Pin_1, g3.Pin_1
  N3: 3_2_1_G_V.pin3, g1.Pin_0, e1.Pin_1
  N4: 3_2_1_G_V.pin4, e2.Pin_1, g2.Pin_0
  N5: 3_2_1_G_V.pin5, g3.Pin_0, e3.Pin_1
  N6: s1.pin2, e1.Pin_0
  N7: s2.pin2, e2.Pin_0
  N8: s3.pin2, e3.Pin_0

notes:
  robot0
